# Fritzing sketch hardware (saved by Fritzing 0.9.0b)
breadboards: 1

parts:
  12V_Fan = DC Motor
  IRF540N = Basic FET N-Channel [package="TO220 [THT]"]
  Arduino_UNO = Arduino Uno (Rev3)
  Servo = Basic Servo
  R1 = Resistor [tolerance=±5% resistance=4.7k package=THT]
  DR1 = PHOTOCELL [package=photocell-kit]
  R2 = Resistor [tolerance=±10% resistance=10k package=THT]
  DHT11 = DHT11 Humitidy and Temperature Sensor
  MOLEX = COMPUTER-PERIPHERAL-POWER [package=computer-peripheral-power-ra]
  IRF540N1 = Basic FET N-Channel [package="TO220 [THT]"]
  LED_Strip = smd LED [color="Red (633nm)" package="1206 [SMD]"]
  R4 = Temperature Sensor (Thermistor) [part_number=NTCLE100E3 package=THT]
  R5 = Resistor [tolerance=±10% resistance=10k package=THT]

nets (from the breadboard view):
  N1: 12V_Fan.pin_1, MOLEX.12V, LED_Strip.anode
  N2: 12V_Fan.pin_2, IRF540N.drain
  N3: IRF540N.gate, Arduino_UNO.D5_PWM
  GND: IRF540N.source, Arduino_UNO.GND, Servo.gnd, R2.Pin_1, DHT11.GND, MOLEX.GND, IRF540N1.source, R5.Pin_1
  N4: Arduino_UNO.A0, DR1.P$2, R2.Pin_0
  N5: Arduino_UNO.A1, R4.pin_1, R5.Pin_0
  N6: Arduino_UNO.D6_PWM, IRF540N1.gate
  N7: Arduino_UNO.D7, R1.Pin_0, DHT11.DATA
  5V: Arduino_UNO.5V, R1.Pin_1, DR1.P$1, DHT11.VDD, R4.pin_0
  VCC: Servo.vcc, MOLEX.5V
  N8: IRF540N1.drain, LED_Strip.cathode

custom parts:
  DHT11 Humitidy and Temperature Sensor: DHT11 Humidity and Temperature Sensor
  Temperature Sensor (Thermistor): A 2.2k NTC Thermistor (Temperature Sensor)
